# Fritzing sketch GpsTracker (saved by Fritzing 0.9.4)

parts:
  microSD1 = MicroSD Card Module
  U2 = GP-2106 [package=gp-2106]
  Součástka1 = Arduino Nano (Rev3.0)
  S4 = Pushbutton [package="[SMD]"]
  LED1 = RGB LED (com. cathode, rbg) [package="5 mm [THT]"]

nets:
  GND: microSD1.GND, U2.GND, Součástka1.GND, S4.Pin_3, S4.Pin_4
  VCC: microSD1.VCC, Součástka1.5V
  N1: U2.1PPS, Součástka1.D2
  N2: Součástka1.D3, LED1.green_anode
  N3: Součástka1.D4, LED1.blue_anode
  N4: Součástka1.D5, LED1.red_anode
  N5: Součástka1.RESET, S4.Pin_1, S4.Pin_2
